// Logisim project 8_Bit_CPU.circ as structural Verilog: 1 circuit, main circuit main
module main (
  input  WRITE_EN,
  input  in_2,
  input  in_3,
  input  in_4,
  input  in_5,
  input  in_6,
  input  in_7,
  input  in_8,
  input  in_9,
  input  in_10,
  input  in_11,
  input  in_12,
  input  in_13,
  input  in_14,
  input  in_15,
  input  in_16,
  input  in_17,
  input  in_18,
  input  in_19,
  input  in_20,
  input  in_21,
  input  in_22,
  input  in_23,
  input  in_24,
  input  in_25,
  input  CTRL_SIGNAL_IN,
  input  CLOCK_IN,
  input  LSB_TO_BUS,
  input  LSB_FROM_BUS,
  input  in_30,
  input  in_31,
  input  in_32,
  input  in_33,
  input  in_34,
  input  in_35,
  input  TOGGLER_DIP_OR_REG,
  input  in_37,
  input  in_38,
  input  in_39,
  input  in_40,
  input  in_41,
  input  in_42,
  input  in_43,
  input  in_44,
  input  in_45,
  input  in_46,
  input  in_47,
  input  in_48,
  output [7:0] out_49
);

  wire A, A1, A3, ADD_IN_sw1, ADD_IN_sw2, ADD_IN_sw3, ADD_IN_sw4, ALU_OUT, and_1_out, BUS_0, BUS_1, BUS_2,
       BUS_3, BUS_4, BUS_5, BUS_6, BUS_7, CLK, CO, IR_4, IR_5, IR_6, IR_7, n74157_1_pin2, n74157_1_pin5,
       n74157_1_pin11, n74157_1_pin14, n74157_1_pin15, n74157_2_pin2, n74157_2_pin5, n74157_2_pin11,
       n74157_2_pin14, n74157_3_pin3, n74157_3_pin6, n74157_3_pin10, n74157_3_pin13, n74157_3_pin15,
       n74157_4_pin3, n74157_4_pin4, n74157_4_pin15, n74163_1_pin9, n74163_2_pin1, n74163_2_pin2,
       n74163_2_pin11, n74241_6_pin12, n74241_6_pin14, n74241_6_pin16, n74241_6_pin18, n74241_7_pin2,
       n74241_8_pin2, n74241_8_pin4, n74241_8_pin6, n74241_8_pin8, n74241_9_pin2, n74241_9_pin4,
       n74241_9_pin6, n74241_9_pin8, n74241_10_pin2, n74241_10_pin3, n74241_10_pin4, n74241_10_pin5,
       n74241_10_pin6, n74241_10_pin7, n74241_10_pin8, n74241_10_pin9, n74241_11_pin2, n74241_12_pin2,
       n74241_12_pin4, n74241_12_pin6, n74241_12_pin8, n74241_13_pin2, n74241_13_pin4, n74241_13_pin6,
       n74241_13_pin8, n74283_1_pin2, n74283_1_pin6, n74283_1_pin9, n74283_1_pin11, n74283_1_pin15,
       n74283_2_pin2, n74283_2_pin6, n74283_2_pin11, n74283_2_pin15, not_2_out, not_3_out, RA1, RA2, RA3,
       RA4, RA5, RA6, RA7, RA8, RB1, RB2, RB3, RB4, RB5, RB6, RB7, RB8, RSET_PC, undriven, undriven_2,
       undriven_3, undriven_4, undriven_5;
  wire [1:0] n74157_2_pin4, n74157_2_pin9, n74157_3_pin4, n74157_3_pin9, n74241_2_pin5, n74241_2_pin9,
       n74241_4_pin5, n74241_4_pin9, n74241_6_pin5, n74241_6_pin9;
  wire [3:0] n74157_1_pin4, n74241_1_pin9, n74241_3_pin9, n74241_5_pin9, register_3_q;
  wire [7:0] register_4_q, rom_1_data, rom_2_data, rom_3_data, rom_4_data, rom_5_data;
  wire [9:7] n74163_2_pin14;

  Clock clock_1 (.out(CLK));
  Register register_1 (
    .D({n74241_2_pin5, n74241_2_pin9, n74241_1_pin9}), .en(in_16), .clk(CLK),
    .Q({RA8, RA7, RA6, RA5, RA4, RA3, RA2, RA1}), .clr(in_3));
  Register register_2 (
    .D({n74241_4_pin5, n74241_4_pin9, n74241_3_pin9}), .en(in_18), .clk(CLK),
    .Q({RB8, RB7, RB6, RB5, RB4, RB3, RB2, RB1}), .clr(in_6));
  Register register_3 (
    .D({n74241_6_pin5, n74241_6_pin9, n74241_5_pin9}), .en(in_20), .clk(CLK),
    .Q({IR_7, IR_6, IR_5, IR_4, register_3_q}), .clr(in_11));
  _74241 u_74241_1 (
    .pin1(A), .pin2(RA1), .pin3(n74241_1_pin9[3]), .pin4(RA2), .pin5(n74241_1_pin9[2]), .pin6(RA3),
    .pin7(n74241_1_pin9[1]), .pin8(RA4), .pin9(n74241_1_pin9[0]), .pin19(in_16), .pin18(BUS_0),
    .pin17(BUS_3), .pin16(BUS_1), .pin15(BUS_2), .pin14(BUS_2), .pin13(BUS_1), .pin12(BUS_3), .pin11(BUS_0));
  _74241 u_74241_2 (
    .pin1(A), .pin2(RA5), .pin3(n74241_2_pin5[1]), .pin4(RA6), .pin5(n74241_2_pin5[0]), .pin6(RA7),
    .pin7(n74241_2_pin9[1]), .pin8(RA8), .pin9(n74241_2_pin9[0]), .pin19(in_16), .pin18(BUS_4),
    .pin17(BUS_7), .pin16(BUS_5), .pin15(BUS_6), .pin14(BUS_6), .pin13(BUS_5), .pin12(BUS_7), .pin11(BUS_4));
  _74241 u_74241_3 (
    .pin1(A1), .pin2(RB1), .pin3(n74241_3_pin9[3]), .pin4(RB2), .pin5(n74241_3_pin9[2]), .pin6(RB3),
    .pin7(n74241_3_pin9[1]), .pin8(RB4), .pin9(n74241_3_pin9[0]), .pin19(in_18), .pin18(BUS_0),
    .pin17(BUS_3), .pin16(BUS_1), .pin15(BUS_2), .pin14(BUS_2), .pin13(BUS_1), .pin12(BUS_3), .pin11(BUS_0));
  _74241 u_74241_4 (
    .pin1(A1), .pin2(RB5), .pin3(n74241_4_pin5[1]), .pin4(RB6), .pin5(n74241_4_pin5[0]), .pin6(RB7),
    .pin7(n74241_4_pin9[1]), .pin8(RB8), .pin9(n74241_4_pin9[0]), .pin19(in_18), .pin18(BUS_4),
    .pin17(BUS_7), .pin16(BUS_5), .pin15(BUS_6), .pin14(BUS_6), .pin13(BUS_5), .pin12(BUS_7), .pin11(BUS_4));
  _74241 u_74241_5 (
    .pin1(A3), .pin2(register_3_q[0]), .pin3(n74241_5_pin9[3]), .pin4(register_3_q[1]),
    .pin5(n74241_5_pin9[2]), .pin6(register_3_q[2]), .pin7(n74241_5_pin9[1]), .pin8(register_3_q[3]),
    .pin9(n74241_5_pin9[0]), .pin19(in_20), .pin18(BUS_0), .pin17(BUS_3), .pin16(BUS_1), .pin15(BUS_2),
    .pin14(BUS_2), .pin13(BUS_1), .pin12(BUS_3), .pin11(BUS_0));
  _74241 u_74241_6 (
    .pin1(A3), .pin2(IR_4), .pin3(n74241_6_pin5[1]), .pin4(IR_5), .pin5(n74241_6_pin5[0]), .pin6(IR_6),
    .pin7(n74241_6_pin9[1]), .pin8(IR_7), .pin9(n74241_6_pin9[0]), .pin19(in_20), .pin18(n74241_6_pin18),
    .pin17(BUS_7), .pin16(n74241_6_pin16), .pin15(BUS_6), .pin14(n74241_6_pin14), .pin13(BUS_5),
    .pin12(n74241_6_pin12), .pin11(BUS_4));
  LED led_1 (.in(n74241_6_pin12));
  LED led_2 (.in(n74241_6_pin14));
  LED led_3 (.in(n74241_6_pin16));
  LED led_4 (.in(n74241_6_pin18));
  LED led_5 (.in(BUS_3));
  LED led_6 (.in(BUS_2));
  LED led_7 (.in(BUS_1));
  LED led_8 (.in(BUS_0));
  _74241 u_74241_7 (
    .pin1(A3), .pin2(n74241_7_pin2), .pin4(n74241_7_pin2), .pin6(n74241_7_pin2), .pin8(n74241_7_pin2),
    .pin18(BUS_4), .pin16(BUS_5), .pin14(BUS_6), .pin12(BUS_7));  // open: pin3, pin5, pin7, pin9, pin19, pin17, pin15, pin13, pin11
  LED LSB_BUS (.in(BUS_0));
  LED led_9 (.in(BUS_1));
  LED led_10 (.in(BUS_2));
  LED led_11 (.in(BUS_3));
  LED led_12 (.in(BUS_4));
  LED led_13 (.in(BUS_5));
  LED led_14 (.in(BUS_6));
  LED MSB_BUS (.in(BUS_7));
  _74241 u_74241_8 (
    .pin1(in_2), .pin2(n74241_8_pin2), .pin4(n74241_8_pin4), .pin6(n74241_8_pin6), .pin8(n74241_8_pin8),
    .pin18(BUS_0), .pin16(BUS_1), .pin14(BUS_2), .pin12(BUS_3));  // open: pin3, pin5, pin7, pin9, pin19, pin17, pin15, pin13, pin11
  _74241 u_74241_9 (
    .pin1(in_2), .pin2(n74241_9_pin2), .pin4(n74241_9_pin4), .pin6(n74241_9_pin6), .pin8(n74241_9_pin8),
    .pin18(BUS_4), .pin16(BUS_5), .pin14(BUS_6), .pin12(BUS_7));  // open: pin3, pin5, pin7, pin9, pin19, pin17, pin15, pin13, pin11
  DipSwitch dipswitch_1 (
    .sw1(n74241_8_pin2), .sw2(n74241_8_pin4), .sw3(n74241_8_pin6), .sw4(n74241_8_pin8), .sw5(n74241_9_pin2),
    .sw6(n74241_9_pin4), .sw7(n74241_9_pin6), .sw8(n74241_9_pin8));
  ROM #(.addrWidth(10)) rom_1 (.addr({in_23, in_22, register_4_q}), .data(rom_1_data));
  _74241 u_74241_10 (
    .pin1(CO), .pin2(n74241_10_pin2), .pin3(n74241_10_pin3), .pin4(n74241_10_pin4), .pin5(n74241_10_pin5),
    .pin6(n74241_10_pin6), .pin7(n74241_10_pin7), .pin8(n74241_10_pin8), .pin9(n74241_10_pin9), .pin19(in_7),
    .pin18(BUS_0), .pin17(BUS_3), .pin16(BUS_1), .pin15(BUS_2), .pin14(BUS_2), .pin13(BUS_1), .pin12(BUS_3),
    .pin11(BUS_0));
  _74241 u_74241_11 (
    .pin1(CO), .pin2(n74241_11_pin2), .pin4(n74241_11_pin2), .pin6(n74241_11_pin2), .pin8(n74241_11_pin2),
    .pin18(BUS_4), .pin16(BUS_5), .pin14(BUS_6), .pin12(BUS_7));  // open: pin3, pin5, pin7, pin9, pin19, pin17, pin15, pin13, pin11
  _74157 u_74157_1 (
    .pin1(TOGGLER_DIP_OR_REG), .pin2(n74157_1_pin2), .pin3(BUS_0), .pin4(n74157_1_pin4[0]),
    .pin5(n74157_1_pin5), .pin6(BUS_1), .pin7(n74157_1_pin4[1]), .pin15(n74157_1_pin15),
    .pin14(n74157_1_pin14), .pin13(BUS_3), .pin12(n74157_1_pin4[3]), .pin11(n74157_1_pin11), .pin10(BUS_2),
    .pin9(n74157_1_pin4[2]));
  _74163 u_74163_1 (
    .pin1(RSET_PC), .pin2(CLK), .pin3(n74241_10_pin9), .pin4(n74241_10_pin7), .pin5(n74241_10_pin5),
    .pin6(n74241_10_pin3), .pin7(in_12), .pin14(n74241_10_pin2), .pin13(n74241_10_pin4),
    .pin12(n74241_10_pin6), .pin11(n74241_10_pin8), .pin10(in_12), .pin9(n74163_1_pin9));  // open: pin15
  LED LSB (.in(BUS_0));
  LED led_15 (.in(BUS_1));
  LED led_16 (.in(BUS_2));
  LED led_17 (.in(BUS_3));
  LED led_18 (.in(BUS_4));
  LED led_19 (.in(BUS_5));
  LED led_20 (.in(BUS_6));
  LED MSB (.in(BUS_7));
  _74241 u_74241_12 (
    .pin1(ALU_OUT), .pin2(n74241_12_pin2), .pin4(n74241_12_pin4), .pin6(n74241_12_pin6),
    .pin8(n74241_12_pin8), .pin18(BUS_0), .pin16(BUS_1), .pin14(BUS_2), .pin12(BUS_3));  // open: pin3, pin5, pin7, pin9, pin19, pin17, pin15, pin13, pin11
  _74241 u_74241_13 (
    .pin1(ALU_OUT), .pin2(n74241_13_pin2), .pin4(n74241_13_pin4), .pin6(n74241_13_pin6),
    .pin8(n74241_13_pin8), .pin18(BUS_4), .pin16(BUS_5), .pin14(BUS_6), .pin12(BUS_7));  // open: pin3, pin5, pin7, pin9, pin19, pin17, pin15, pin13, pin11
  not not_1 (n74163_1_pin9, in_7);
  _7_Segment_Display u_7_segment_display_1 (
    .g(rom_1_data[6]), .f(rom_1_data[5]), .a(rom_1_data[0]), .b(rom_1_data[1]), .e(rom_1_data[4]),
    .d(rom_1_data[3]), .c(rom_1_data[2]), .dp(undriven));
  _74157 u_74157_2 (
    .pin1(TOGGLER_DIP_OR_REG), .pin2(n74157_2_pin2), .pin3(BUS_4), .pin4(n74157_2_pin4[0]),
    .pin5(n74157_2_pin5), .pin6(BUS_5), .pin7(n74157_2_pin4[1]), .pin15(n74157_1_pin15),
    .pin14(n74157_2_pin14), .pin13(BUS_7), .pin12(n74157_2_pin9[1]), .pin11(n74157_2_pin11), .pin10(BUS_6),
    .pin9(n74157_2_pin9[0]));
  _74283 u_74283_1 (
    .pin1(n74241_12_pin4), .pin2(n74283_1_pin2), .pin3(RA2), .pin4(n74241_12_pin2), .pin5(RA1),
    .pin6(n74283_1_pin6), .pin7(in_8), .pin15(n74283_1_pin15), .pin14(RA3), .pin13(n74241_12_pin6),
    .pin12(RA4), .pin11(n74283_1_pin11), .pin10(n74241_12_pin8), .pin9(n74283_1_pin9));
  xor xor_1 (n74283_1_pin6, RB1, in_8);
  DipSwitch DATA_IN (
    .sw1(n74157_1_pin2), .sw2(n74157_1_pin5), .sw3(n74157_1_pin11), .sw4(n74157_1_pin14),
    .sw5(n74157_2_pin2), .sw6(n74157_2_pin5), .sw7(n74157_2_pin11), .sw8(n74157_2_pin14));
  xor xor_2 (n74283_1_pin2, RB2, in_8);
  xor xor_3 (n74283_1_pin15, RB3, in_8);
  ROM #(.addrWidth(10)) rom_2 (.addr({in_23, in_22, register_4_q}), .data(rom_2_data));
  xor xor_4 (n74283_1_pin11, RB4, in_8);
  Register register_4 (
    .D({BUS_7, BUS_6, BUS_5, BUS_4, BUS_3, BUS_2, BUS_1, BUS_0}), .en(in_24), .clk(and_1_out),
    .Q(register_4_q));  // open: clr
  and and_1 (and_1_out, CLK, in_25);
  DipSwitch #(.number(4)) ADD_IN (.sw1(ADD_IN_sw1), .sw2(ADD_IN_sw2), .sw3(ADD_IN_sw3), .sw4(ADD_IN_sw4));
  _74283 u_74283_2 (
    .pin1(n74241_13_pin4), .pin2(n74283_2_pin2), .pin3(RA6), .pin4(n74241_13_pin2), .pin5(RA5),
    .pin6(n74283_2_pin6), .pin7(n74283_1_pin9), .pin15(n74283_2_pin15), .pin14(RA7), .pin13(n74241_13_pin6),
    .pin12(RA8), .pin11(n74283_2_pin11), .pin10(n74241_13_pin8));  // open: pin9
  xor xor_5 (n74283_2_pin6, RB5, in_8);
  _74157 u_74157_3 (
    .pin1(TOGGLER_DIP_OR_REG), .pin2(ADD_IN_sw1), .pin3(n74157_3_pin3), .pin4(n74157_3_pin4[0]),
    .pin5(ADD_IN_sw2), .pin6(n74157_3_pin6), .pin7(n74157_3_pin4[1]), .pin15(n74157_3_pin15),
    .pin14(ADD_IN_sw4), .pin13(n74157_3_pin13), .pin12(n74157_3_pin9[1]), .pin11(ADD_IN_sw3),
    .pin10(n74157_3_pin10), .pin9(n74157_3_pin9[0]));
  xor xor_6 (n74283_2_pin2, RB6, in_8);
  xor xor_7 (n74283_2_pin15, RB7, in_8);
  not not_2 (not_2_out, in_15);
  ROM #(.addrWidth(11)) rom_3 (
    .addr({in_47, n74163_2_pin14, in_46, in_44, in_42, in_41, in_40, in_39, in_38}), .data(rom_3_data));
  xor xor_8 (n74283_2_pin11, RB8, in_8);
  _74157 u_74157_4 (
    .pin1(not_2_out), .pin2(in_15), .pin3(n74157_4_pin3), .pin4(n74157_4_pin4), .pin15(n74157_4_pin15));  // open: pin5, pin6, pin7, pin14, pin13, pin12, pin11, pin10, pin9
  LED LSB_ADR_REG (.in(n74157_3_pin4[0]));
  LED led_21 (.in(n74157_3_pin4[1]));
  LED led_22 (.in(n74157_3_pin9[0]));
  LED MSB_ADR_REG (.in(n74157_3_pin9[1]));
  _74175 u_74175_1 (
    .pin1(in_35), .pin2(n74157_3_pin3), .pin4(BUS_0), .pin5(BUS_1), .pin7(n74157_3_pin6),
    .pin15(n74157_3_pin13), .pin13(BUS_3), .pin12(BUS_2), .pin10(n74157_3_pin10), .pin9(CLK));  // open: pin3, pin6, pin14, pin11
  _7_Segment_Display u_7_segment_display_2 (
    .g(rom_2_data[6]), .f(rom_2_data[5]), .a(rom_2_data[0]), .b(rom_2_data[1]), .e(rom_2_data[4]),
    .d(rom_2_data[3]), .c(rom_2_data[2]), .dp(undriven_2));
  and and_2 (n74157_4_pin3, CTRL_SIGNAL_IN, CLOCK_IN);
  ROM #(.addrWidth(10)) rom_4 (.addr({in_23, in_22, register_4_q}), .data(rom_4_data));
  _7_Segment_Display u_7_segment_display_3 (
    .g(rom_3_data[6]), .f(rom_3_data[5]), .a(rom_3_data[0]), .b(rom_3_data[1]), .e(rom_3_data[4]),
    .d(rom_3_data[3]), .c(rom_3_data[2]), .dp(undriven_3));
  _7_Segment_Display u_7_segment_display_4 ();  // open: g, f, a, b, e, d, c, dp
  _7_Segment_Display u_7_segment_display_5 (.g(in_37));  // open: f, a, b, e, d, c, dp
  _7_Segment_Display u_7_segment_display_6 ();  // open: g, f, a, b, e, d, c, dp
  RAM ram_1 (
    .addr({in_34, in_33, in_32, in_31, n74157_3_pin9, n74157_3_pin4}), .we(n74157_4_pin4), .oe(in_14),
    .clk(CLK), .din({n74157_2_pin9, n74157_2_pin4, n74157_1_pin4}), .dout(out_49));
  not not_3 (not_3_out, in_14);
  _74163 u_74163_2 (
    .pin1(n74163_2_pin1), .pin2(n74163_2_pin2), .pin7(in_48), .pin14(n74163_2_pin14[7]),
    .pin13(n74163_2_pin14[8]), .pin12(n74163_2_pin14[9]), .pin11(n74163_2_pin11), .pin10(in_43), .pin9(in_45));  // open: pin3, pin4, pin5, pin6, pin15
  _7_Segment_Display u_7_segment_display_7 (
    .g(rom_4_data[6]), .f(rom_4_data[5]), .a(rom_4_data[0]), .b(rom_4_data[1]), .e(rom_4_data[4]),
    .d(rom_4_data[3]), .c(rom_4_data[2]), .dp(undriven_4));
  Clock clock_2 (.out(n74163_2_pin2));
  not not_4 (A, in_17);
  not not_5 (A3, in_21);
  _74241 u_74241_14 (
    .pin1(not_3_out), .pin2(out_49[0]), .pin4(out_49[1]), .pin6(out_49[2]), .pin8(out_49[3]), .pin18(BUS_0),
    .pin16(BUS_1), .pin14(BUS_2), .pin12(BUS_3));  // open: pin3, pin5, pin7, pin9, pin19, pin17, pin15, pin13, pin11
  not not_6 (n74163_2_pin1, n74163_2_pin11);
  not not_7 (CO, in_10);
  not not_8 (RSET_PC, in_13);
  not not_9 (A1, in_19);
  ROM #(.addrWidth(10)) rom_5 (.addr({in_23, in_22, register_4_q}), .data(rom_5_data));
  _74241 u_74241_15 (
    .pin1(not_3_out), .pin2(out_49[4]), .pin4(out_49[5]), .pin6(out_49[6]), .pin8(out_49[7]), .pin18(BUS_4),
    .pin16(BUS_5), .pin14(BUS_6), .pin12(BUS_7));  // open: pin3, pin5, pin7, pin9, pin19, pin17, pin15, pin13, pin11
  not not_10 (ALU_OUT, in_9);
  _7_Segment_Display u_7_segment_display_8 (
    .g(rom_5_data[6]), .f(rom_5_data[5]), .a(rom_5_data[0]), .b(rom_5_data[1]), .e(rom_5_data[4]),
    .d(rom_5_data[3]), .c(rom_5_data[2]), .dp(undriven_5));
  // also tied to GND on the sheet: {n74241_7_pin2, n74241_11_pin2, n74157_1_pin15, n74157_3_pin15, n74157_4_pin15}

  // Other names for the same wires on the sheet: ADD_SUB = in_8; B = in_16; B1 = in_18; B3 = in_20; COUNT_EN = in_12;
  //   JUMP_LOAD = in_7; RAM_IN = in_15; RAM_OUT = in_14

  // Notes on the sheet:
  //   REG B
  //   REG A
  //   IR
  //   lsb_hh
  //   JUMP/LOAD
  //   contents of rom_1 (hex, n*v repeats v):
  //   384*3f 128*40
  //   PROGRAM COUNTER
  //   COUNT_OUT_EN_(ACT_0)
  //   contents of rom_2 (hex, n*v repeats v):
  //   100*3f 100*6 56*5b 100*3f 57*6 99*3f
  //   ALU
  //   contents of rom_3 (hex, n*v repeats v):
  //   40 6 5b 4f 66 6d 7d 7 7f 6f 77 7c 39 5e 79 71
  //   RAM DIVISION
  //   ADDRESS_REG
  //   contents of rom_4 (hex, n*v repeats v):
  //   10*3f 10*6 10*5b 10*4f 10*66 10*6d 10*7d 10*7 10*7f 10*6f 10*3f 10*6 10*5b 10*4f 10*66 10*6d 10*7d
  //   10*7 10*7f 10*6f 10*3f 10*6 10*5b 10*4f 10*66 6*6d 10*3f 10*6 10*5b 10*4f 10*66 10*6d 10*7d 10*7
  //   10*7f 10*6f 10*3f 10*6 17*5b 10*6 10*3f 10*6f 10*7f 10*7 10*7d 10*6d 10*66 10*4f 10*5b 10*6 9*3f
  //   IN
  //   OUT
  //   OUT
  //   IN
  //   OUT
  //   PROGRAM COUNTER
  //   REG A
  //   REG B
  //   IN
  //   INSTRUCTION REG 
  //   CONTROL LOGIC
  //   contents of rom_5 (hex, n*v repeats v):
  //   3f 6 5b 4f 66 6d 7d 7 7f 6f 3f 6 5b 4f 66 6d 7d 7 7f 6f 3f 6 5b 4f 66 6d 7d 7 7f 6f 3f 6 5b 4f 66 6d
  //   7d 7 7f 6f 3f 6 5b 4f 66 6d 7d 7 7f 6f 3f 6 5b 4f 66 6d 7d 7 7f 6f 3f 6 5b 4f 66 6d 7d 7 7f 6f 3f 6
  //   5b 4f 66 6d 7d 7 7f 6f 3f 6 5b 4f 66 6d 7d 7 7f 6f 3f 6 5b 4f 66 6d 7d 7 7f 6f 3f 6 5b 4f 66 6d 7d 7
  //   7f 6f 3f 6 5b 4f 66 6d 7d 7 7f 6f 3f 6 5b 4f 66 6d 7d 7 7f 6f 3f 6 5b 4f 66 6d 7d 7 7f 6f 3f 6 5b 4f
  //   66 6d 7d 7 7f 6f 3f 6 5b 4f 66 6d 7d 7 7f 6f 3f 6 5b 4f 66 6d 7d 7 7f 6f 3f 6 5b 4f 66 6d 7d 7 7f 6f
  //   3f 6 5b 4f 66 6d 7d 7 7f 6f 3f 6 5b 4f 66 6d 7d 7 7f 6f 3f 6 5b 4f 66 6d 7d 7 7f 6f 3f 6 5b 4f 66 6d
  //   7d 7 7f 6f 3f 6 5b 4f 66 6d 7d 7 7f 6f 3f 6 5b 4f 66 6d 7d 7 7f 6f 3f 6 5b 4f 66 6d 7d 7 7f 6f 3f 6
  //   5b 4f 66 6d 3f 6 5b 4f 66 6d 7d 7 7f 6f 3f 6 5b 4f 66 6d 7d 7 7f 6f 3f 6 5b 4f 66 6d 7d 7 7f 6f 3f 6
  //   5b 4f 66 6d 7d 7 7f 6f 3f 6 5b 4f 66 6d 7d 7 7f 6f 3f 6 5b 4f 66 6d 7d 7 7f 6f 3f 6 5b 4f 66 6d 7d 7
  //   7f 6f 3f 6 5b 4f 66 6d 7d 7 7f 6f 3f 6 5b 4f 66 6d 7d 7 7f 6f 3f 6 5b 4f 66 6d 7d 7 7f 6f 3f 6 5b 4f
  //   66 6d 7d 7 7f 6f 3f 6 5b 4f 66 6d 7d 7 7f 6f 3f 6 5b 4f 66 6d 7d 7 7f 7 7d 6d 66 4f 5b 6 3f 6f 7f 7
  //   7d 6d 66 4f 5b 6 3f 6f 7f 7 7d 6d 66 4f 5b 6 3f 6f 7f 7 7d 6d 66 4f 5b 6 3f 6f 7f 7 7d 6d 66 4f 5b 6
  //   3f 6f 7f 7 7d 6d 66 4f 5b 6 3f 6f 7f 7 7d 6d 66 4f 5b 6 3f 6f 7f 7 7d 6d 66 4f 5b 6 3f 6f 7f 7 7d 6d
  //   66 4f 5b 6 3f 6f 7f 7 7d 6d 66 4f 5b 6 3f 6f 7f 7 7d 6d 66 4f 5b 6 3f 6f 7f 7 7d 6d 66 4f 5b 6 3f 6f
  //   7f 7 7d 6d 66 4f 5b 6
  //   OUT
  //   ADD_0/SUB_1
  //    ALU
  //    RAM
endmodule
